# Fritzing sketch DHT11-sensor-schematic (saved by Fritzing 0.9.3b)
breadboards: 1

parts:
  Arduino_Uno = Arduino Uno (R4)
  CAM2 = ESP32 - CAM
  DHT11 = Humidity and Temperature Sensor DHT11
  switch = SWITCH_SPDT [package=kps-1290]

nets:
  GND: Arduino_Uno.GND, Arduino_Uno.RESET, CAM2.GND, DHT11.GND_2, switch.P
  N1: Arduino_Uno.D0/RX, CAM2.VOR
  N2: Arduino_Uno.D1/TX, CAM2.VOT
  3V3: Arduino_Uno.3V3, DHT11.Vcc
  5V: Arduino_Uno.5V, CAM2.5V
  N3: CAM2.IO0, switch.O
  N4: CAM2.IO16, DHT11.Data-signal

custom parts:
  Arduino Uno (R4): The Arduino Uno is a microcontroller board based on the ATmega328 (datasheet). It has 14 digital input/output pins (of which 6 can be used as PWM outputs), 6 analog inputs, a 16 MHz ceramic resonator, a USB connection, a power jack, an ICSP header, and a reset button. It contains everything needed to support the microcontroller; simply connect it to a computer with a USB cable or power it with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
  ESP32 - CAM: The ESP32-CAM has a very competitive small-size camera module that can operate independently as a minimum system with a footprint of only 27*40.5*4.5mm and a deep sleep current of up to 6mA.
  Humidity and Temperature Sensor DHT11: Digital relative humidity & temperature sensor DHT11
