# Fritzing sketch schematic(v5.a) (saved by Fritzing 0.9.3b)
breadboards: 1

parts:
  TILT1 = Basic Servo
  PAN1 = Basic Servo
  CAM1 = ESP32 - CAM
  Motor_Driver_(MD1) = L298 [package=multiwatt15]
  M4 = DC Motor
  M3 = DC Motor
  M2 = DC Motor
  M1 = DC Motor
  V1 = DC Power [voltage=12V]

nets:
  GND: TILT1.gnd, PAN1.gnd, CAM1.GND, Motor_Driver_(MD1).GND, V1.V-
  5V: TILT1.vcc, PAN1.vcc, CAM1.5V
  N1: TILT1.pulse, CAM1.IO16
  N2: PAN1.pulse, CAM1.IO4
  N3: CAM1.IO12, Motor_Driver_(MD1).ENA, Motor_Driver_(MD1).ENB
  N4: CAM1.IO13, Motor_Driver_(MD1).IN1
  N5: CAM1.IO15, Motor_Driver_(MD1).IN2
  N6: CAM1.IO14, Motor_Driver_(MD1).IN3
  N7: CAM1.IO2, Motor_Driver_(MD1).IN4
  N8: Motor_Driver_(MD1).OUT1, M3.pin_1, M1.pin_1
  N9: Motor_Driver_(MD1).OUT2, M3.pin_2, M1.pin_2
  12V: Motor_Driver_(MD1).VS, V1.V+
  N10: Motor_Driver_(MD1).OUT3, M4.pin_1, M2.pin_1
  N11: Motor_Driver_(MD1).OUT4, M4.pin_2, M2.pin_2

custom parts:
  Basic Servo: A generic servo.
  ESP32 - CAM: The ESP32-CAM has a very competitive small-size camera module that can operate independently as a minimum system with a footprint of only 27*40.5*4.5mm and a deep sleep current of up to 6mA.
