# Fritzing sketch schematic(v5.b) (saved by Fritzing 0.9.3b)
breadboards: 1

parts:
  LM1 = LM35 Temperature Sensor [package="TO92 [THT]"]
  U1 = Arduino Uno (Rev3)
  DHT1 = Humidity and Temperature Sensor DHT11
  V2 = DC Power [voltage=5V]

nets:
  5V: LM1.+Vs, U1.5V, DHT1.Vcc, V2.V+
  N1: LM1.Vout, U1.A2
  GND: LM1.GND, U1.GND, DHT1.GND, V2.V-
  N2: U1.D4, DHT1.Data

notes:
  to replace R3
  using Arduino Uno R4
  +
  9-in-1 shield
  9-in-1 shield Physical attached to Uno R4

custom parts:
  Humidity and Temperature Sensor DHT11: Digital relative humidity & temperature sensor DHT11
