# Fritzing sketch schematic(v5.b-dht11 only) (saved by Fritzing 0.9.3b)
breadboards: 1

parts:
  U1 = Arduino Uno (Rev3)
  DHT1 = Humidity and Temperature Sensor DHT11
  V2 = DC Power [voltage=5V]

nets:
  GND: U1.GND, DHT1.GND, V2.V-
  N1: U1.D4, DHT1.Data
  5V: U1.5V, DHT1.Vcc, V2.V+

notes:
  to replace R3
  using Arduino Uno R4
  +
  9-in-1 shield
  9-in-1 shield Physical attached to Uno R4

custom parts:
  Humidity and Temperature Sensor DHT11: Digital relative humidity & temperature sensor DHT11
